# Fritzing sketch Push_button (saved by Fritzing 0.9.2b)
breadboards: 1

parts:
  Switch = Round Pushbutton
  Raspberry_Pi = Raspberry Pi 2

nets:
  N1: Switch.leg0, Raspberry_Pi.GPIO5
  N2: Switch.leg1, Raspberry_Pi.GND
